# Fritzing sketch BabyMonitor (saved by Fritzing 0.9.3b)

parts:
  Part1 = Arduino Pro Mini (3.3V)
  Part2 = Bluetooth HM-10
  Part3 = Breakout Board for Electret Microphone

nets:
  N1: Part1.A3, Part3.AUD
  N2: Part1.D8, Part2.BRK
  N3: Part1.D7, Part2.RXD
