# Fritzing sketch FlowerWatering (saved by Fritzing 0.9.3b)

parts:
  Part1 = FC-28 Soil Hygrometer Module
  Part2 = FC-28 Soil Hygrometer Module - Probe
  Part3 = Bluetooth HM-10
  Part4 = Arduino Pro Mini (5V)
  M1 = DC Motor
  Q1 = MOSFET-NCHANNEL [package=to220v]
  VCC2 = 4 x AAA Battery Mount

nets:
  N1: Part1.VCC, Part4.MISO
  N2: Part1.AO, Part4.A2
  N3: Part1.POS, Part2.POS
  N4: Part1.NEG, Part2.NEG
  N5: Part3.RXD, Part4.MOSI
  N6: Part3.BRK, Part4.D10
  N7: M1.pin_2, Q1.D
  N8: Q1.S, VCC2.-

notes:
  + -
  P8
  JDY-08
  Pro Mini

custom parts:
  FC-28 Soil Hygrometer Module: The FC-28 is a soil hygrometer module that uses the Texas Instruments LM393 comparator chip to provide an analog measurement of soil humidity. The digital output is high when soil moisture is over a certain threshold, as determined by adjusting the potentiometer.
  FC-28 Soil Hygrometer Module - Probe: The FC-28 is a soil hygrometer module that uses the Texas Instruments LM393 comparator chip to provide an analog measurement of soil humidity.
