# Fritzing sketch HouseGarden (saved by Fritzing 0.9.3b)

parts:
  Part1 = FC-28 Soil Hygrometer Module
  Part2 = FC-28 Soil Hygrometer Module - Probe
  Part3 = Bluetooth HM-10
  Part4 = Arduino Pro Mini (5V)
  M1 = DC Motor
  Q2 = NPN-Transistor [package="TO92 [THT]"]
  R1 = Resistor [tolerance=±5% resistance=220 package="0402 [SMD]"]
  Part5 = FC-28 Soil Hygrometer Module
  Part6 = FC-28 Soil Hygrometer Module - Probe
  Part7 = FC-28 Soil Hygrometer Module
  Part8 = FC-28 Soil Hygrometer Module - Probe
  Part9 = ACS712 Low Current Sensor Board v12
  LED2 = LEDs [package=led10mm]
  U2 = RELAY-SOLIDSTATE [package=relay-s108t02]
  HLK-PM3 = HLK-PM12 [part_number=HLK-PM12]
  Q3 = NPN-Transistor [package="TO92 [THT]"]
  R2 = Resistor [tolerance=±5% resistance=220 package="0402 [SMD]"]  # not connected
  M2 = DC Motor
  Q4 = NPN-Transistor [package="TO92 [THT]"]
  R3 = Resistor [tolerance=±5% resistance=220 package="0402 [SMD]"]  # not connected
  M3 = DC Motor

nets:
  N1: Part1.VCC, Part4.MISO
  N2: Part1.AO, Part4.A2
  N3: Part1.POS, Part2.POS
  N4: Part1.NEG, Part2.NEG
  N5: Part3.RXD, Part4.MOSI
  N6: Part3.BRK, Part4.D10
  N7: Part4.A1, Part5.AO
  N8: Part4.A0, Part7.AO
  N9: Part4.SCK, Q2.C, R1.Pin_0
  N10: Part4.D9, Q3.C
  N11: Part4.D8, Q4.C
  N12: M1.pin_2, Q2.E
  N13: Part5.POS, Part6.POS
  N14: Part5.NEG, Part6.NEG
  N15: Part7.POS, Part8.POS
  N16: Part7.NEG, Part8.NEG
  N17: Part9.IP+, U2.T2
  N18: Part9.IP-, LED2.A
  N19: LED2.C, HLK-PM3.AC_1
  N20: U2.T1, HLK-PM3.AC_2
  N21: HLK-PM3.+Vo, M3.pin_1
  N22: Q3.E, M2.pin_2
  N23: Q4.E, M3.pin_2

notes:
  IO1
  JDY-08
  Pro Mini
  IO3
  IO2
  IO4

custom parts:
  FC-28 Soil Hygrometer Module: The FC-28 is a soil hygrometer module that uses the Texas Instruments LM393 comparator chip to provide an analog measurement of soil humidity. The digital output is high when soil moisture is over a certain threshold, as determined by adjusting the potentiometer.
  FC-28 Soil Hygrometer Module - Probe: The FC-28 is a soil hygrometer module that uses the Texas Instruments LM393 comparator chip to provide an analog measurement of soil humidity.
  LEDs: LEDs Standard schematic elements and footprints for 5mm, 3mm, 1206, and 0603 sized LEDs. 5mm - Spark Fun Electronics SKU : COM-00529 (and others)
