# Fritzing sketch Luxmeter (saved by Fritzing 0.9.3b)

parts:
  Part3 = Bluetooth HM-10
  Part4 = Arduino Pro Mini (5V)
  Part5 = BH1750

nets:
  N1: Part3.RXD, Part4.MOSI
  N2: Part3.BRK, Part4.D10
  N3: Part4.A4, Part5.SDA
  N4: Part4.A5, Part5.SCL

custom parts:
  BH1750: Light Sensor
