# Fritzing sketch Meteostation (saved by Fritzing 0.9.3b)

parts:
  Part3 = Bluetooth HM-10
  Part4 = Arduino Nano (Rev3.0)
  Part5 = Altitude/Pressure Sensor - MPL3115A2 Breakout [part_number=SEN-11084]
  U1 = GAS_SENSOR [package=mq-3]

nets:
  N1: Part3.RXD, Part4.D11/MOSI
  N2: Part3.BRK, Part4.D10
  N3: Part4.A6, U1.A1
  N4: Part4.A5, Part5.SCL
  N5: Part4.A4, Part5.SDA
