# Fritzing sketch OrangePiTTL (saved by Fritzing 0.9.3b)

parts:
  Часть1 = Arduino Nano (Rev3.0)
  Orange_Pi_One1 = Orange Pi One [part_number=OPI-ONE]

nets:
  N1: Часть1.D1/TX, Orange_Pi_One1.GND
  N2: Часть1.D0/RX, Orange_Pi_One1.RX
  N3: Часть1.GND, Часть1.RESET, Orange_Pi_One1.TX

custom parts:
  Orange Pi One: It’s an open-source single-board computer. It can run Android 4.4, Ubuntu, Debian, Rasberry Pi Image, as well as the banana pi Image. It uses the AllWinner H3 SoC, and has 512MB DDR3 SDRAM
