# Fritzing sketch ProMiniTTL (saved by Fritzing 0.9.3b)

parts:
  Часть1 = Arduino Nano (Rev3.0)
  Part1 = Arduino Pro Mini (3.3V)

nets:
  N1: Часть1.D1/TX, Part1.TXO
  N2: Часть1.D0/RX, Part1.RXI
  GND: Часть1.GND, Часть1.RESET, Part1.GND
