# Fritzing sketch Relay-JDY-08 (saved by Fritzing 0.9.3b)

parts:
  Часть1 = Bluetooth HM-10
  KY-1 = Keyes Relay [package=THT]
  HLK-PM1 = HLK-PM12 [part_number=HLK-PM12]
  LED4 = LEDs [package=led10mm]
  Part3 = Lilypad Battery Connect

nets:
  N1: Часть1.GND, KY-1.ground, HLK-PM1.-Vo
  N2: Часть1.VCC, KY-1.signal, HLK-PM1.+Vo
  N3: KY-1.C, HLK-PM1.AC_1, Part3.+
  N4: KY-1.NO, LED4.A
  N5: HLK-PM1.AC_2, LED4.C, Part3.-

notes:
  220V AC
  P8

custom parts:
  Keyes Relay: The Keyes 5V relay module is suitable for SCM development, home appliance control. It uses a 5V~12V TIL control signal which can control DC / AC signal.
