# Fritzing sketch SensorSwitch (saved by Fritzing 0.9.3b)

parts:
  Part1 = Arduino Pro Mini (3.3V)
  U1 = TTP223 [package=sot23-6]
  U2 = FS1000A - 433Mhz RF Transmitter [package=THT]
  LED1 = smd LED [color="Red (633nm)" package="1206 [SMD]"]

nets:
  N1: Part1.MISO, U2.DATA
  N2: Part1.D4, U1.Vss
  N3: Part1.D3, LED1.anode

custom parts:
  TTP223: Touch Sensor
  FS1000A - 433Mhz RF Transmitter: This is 433Mhz RF transmitter with receiver kit for Arduino ARM MCU wireless Application environment: Remote control switch, receiver module, motorcycles, automobile anti-theft products, home security products, electric doors, shutter doors, windows, remote control socket, remote control LED, remote audio remote control electric doors, garage door remote control, remote control retractable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
