# Fritzing sketch SmartSocket (saved by Fritzing 0.9.3b)

parts:
  Part3 = Bluetooth HM-10
  HLK-PM2 = HLK-PM12 [part_number=HLK-PM12]  # not connected
  U1 = RELAY-SOLIDSTATE [package=relay-s108t02]
  Part5 = ACS712 Low Current Sensor Board v12
  Part4 = Arduino Pro Mini (5V)
  LED2 = LEDs [package=led10mm]

nets:
  N1: Part3.RXD, Part4.MOSI
  N2: Part3.BRK, Part4.D10
  N3: U1.T1, Part5.IP-
  N4: Part5.IP+, LED2.C
  N5: Part5.VO, Part4.A1

notes:
  ~220

custom parts:
  LEDs: LEDs Standard schematic elements and footprints for 5mm, 3mm, 1206, and 0603 sized LEDs. 5mm - Spark Fun Electronics SKU : COM-00529 (and others)
