# Fritzing sketch TTL (saved by Fritzing 0.9.3b)

parts:
  Часть1 = Arduino Nano (Rev3.0)
  Часть2 = Bluetooth HM-10

nets:
  N1: Часть1.D2, Часть2.TXD
  N2: Часть1.D3, Часть2.RXD
  GND: Часть1.GND, Часть2.GND
  5V: Часть1.5V, Часть2.VCC
