# Fritzing sketch binarySensorJDY08MotionDetector (saved by Fritzing 0.9.3b)

parts:
  PIR1 = PIR sensor
  Part1 = Bluetooth HM-10
  Digispark1 = Digispark
  VCC1 = 4 x AAA Battery Mount

nets:
  VCC: PIR1.VDD, Part1.VCC, Digispark1.VCC, VCC1.+
  N1: PIR1.SIG, Digispark1.P2
  GND: PIR1.GND, Part1.GND, Digispark1.GND, VCC1.-
  N2: Part1.RXD, Digispark1.P1
  N3: Part1.BRK, Digispark1.P0

custom parts:
  Digispark: The Digispark is an Attiny85 based microcontroller development board similar to the Arduino line, only cheaper, smaller, and a bit less powerful. With a whole host of shields to extend its functionality and the ability to use the familiar Arduino IDE the Digispark is a great way to jump into electronics, or perfect for when an Arduino is too big or too much.
