# Fritzing sketch sensor-cc41-a (saved by Fritzing 0.9.3b)

parts:
  Часть1 = Bluetooth HM-10
  VCC1 = Battery
  Часть5 = FC-28 Soil Hygrometer Module - Probe
  Часть6 = FC-28 Soil Hygrometer Module
  Digispark1 = Digispark

nets:
  N1: Часть1.RXD, Digispark1.P1
  GND: Часть1.GND, VCC1.-, Часть6.GND, Digispark1.GND
  VCC: Часть1.VCC, VCC1.+, Digispark1.VCC
  N2: Часть5.POS, Часть6.POS
  N3: Часть5.NEG, Часть6.NEG
  N4: Часть6.VCC, Digispark1.P0
  N5: Часть6.AO, Digispark1.P4

custom parts:
  FC-28 Soil Hygrometer Module - Probe: The FC-28 is a soil hygrometer module that uses the Texas Instruments LM393 comparator chip to provide an analog measurement of soil humidity.
  FC-28 Soil Hygrometer Module: The FC-28 is a soil hygrometer module that uses the Texas Instruments LM393 comparator chip to provide an analog measurement of soil humidity. The digital output is high when soil moisture is over a certain threshold, as determined by adjusting the potentiometer.
  Digispark: The Digispark is an Attiny85 based microcontroller development board similar to the Arduino line, only cheaper, smaller, and a bit less powerful. With a whole host of shields to extend its functionality and the ability to use the familiar Arduino IDE the Digispark is a great way to jump into electronics, or perfect for when an Arduino is too big or too much.
